// Logisim project Piplining.circ as structural Verilog: 16 circuits, main circuit main
module main (
  input  in_1,
  input  in_2,
  input  in_3,
  input  in_4,
  input  in_5,
  output [31:0] R0,
  output [31:0] out_7,
  output [31:0] out_8,
  output [31:0] out_9,
  output [31:0] out_10,
  output [31:0] out_11,
  output [31:0] out_12,
  output [31:0] out_13,
  output [2:0] out_14
);

  wire ALU_SRC, ALU_SRC_EX, B, B_EX, Br_MEM, CLK, J, J_EX, JR, JR_EX, MEM_R, MEM_R_EX, MEM_R_MEM, MEM_W,
       MEM_W_EX, MEM_W_MEM, reg1, reg1_ID, reg2, reg2_ID, reg3, reg3_EX, reg3_ID, RW, RW_EX, RW_MEM,
       Zero_flag;
  wire [1:0] func, func_EX, func_ID, IMM, IMM_EX, IMM_MEM;
  wire [2:0] _1, _1_ID, _2, _2_ID, _3, _3_ID, multiplexer_1_out, multiplexer_2_out;
  wire [3:0] WB, WB_EX, WB_MEM, WB_WB;
  wire [4:0] ALUOP, ALUOP_EX, IMM5_EX, IMM5_ID, IMM5_MEM, OP_CODE, OP_CODE_EX, OP_CODE_ID;
  wire [7:0] IMM8_EX, IMM8_ID, IMM8_MEM;
  wire [10:0] IMM_11_EX, IMM_11_ID, IMM_11_MEM;
  wire [19:0] adder_2_out, adder_3_out, adder_4_out, bit_extender_1_out, bit_extender_2_out,
       bit_extender_3_out, bit_extender_4_out, IMM_PC, IMM_PC_EX, IMM_PC_ID, IMM_PC_MEM, multiplexer_4_out,
       multiplexer_6_out, multiplexer_7_out, NEXT_PC, PC_4, PC_4_EX, PC_4_ID, PC_4_MEM;
  wire [31:0] ALU, ALU_MEM, ALU_WB, bit_extender_5_out, bus_a, bus_a_EX, bus_a_MEM, bus_b, bus_b_EX,
       bus_b_MEM, immediate_value_1_to_alu, JALR_IN, JALR_IN_WB, MEM_RES, MEM_RES_WB, multiplexer_5_out, RB,
       SET_EX, SET_MEM, SET_WB, SSET_OUT, SSET_OUT_WB;

  Clock u_CLK (.out(CLK));
  Register #(.width(20)) PC (.D(NEXT_PC), .en(1'b1), .Q(IMM_PC), .clk(CLK), .clr(in_1));
  RAM #(.addrWidth(20), .dataWidth(16)) ram_1 (
    .addr(IMM_PC), .data({OP_CODE, _3, _1, _2, func}), .sel(1'b1), .clk(CLK), .ld(1'b1), .clr(in_2));
  IF_ID if_id_1 (
    .IMM_PC(PC_4), .IMM_pc___4(IMM_PC), ._1(_1), ._2(_2), ._3(_3), .IMM_pc_2(PC_4_ID),
    .IMM_pc___4_2(IMM_PC_ID), ._1_2(_1_ID), ._2_2(_2_ID), ._3_2(_3_ID), .clk(CLK), .clr(in_3), .reg_1(reg3),
    .reg_1_2(reg3_ID), .reg_2(reg2), .reg_2_2(reg2_ID), .reg_3(reg1), .reg_3_2(reg1_ID), .WB(OP_CODE),
    .WB_2(OP_CODE_ID), .imm_11({_3, _1, _2, func}), .imm_11_2(IMM_11_ID), .imm_8({_1, _2, func}),
    .imm_8_2(IMM8_ID), .imm5({_2, func}), .imm5_2(IMM5_ID), .fun(func), .fun_2(func_ID));
  control_unit control_unit_1 (
    .ALUop(ALUOP), .ALU_SRC(ALU_SRC), .JR(JR), .J(J), .B(B), .MEM_W(MEM_W), .MEM_R(MEM_R), .RW(RW), .WB(WB),
    .IMM(IMM), .W(reg3), .Opcode(OP_CODE_ID), .R2(reg2), .R1(reg1));
  Multiplexer #(.width(3), .enable("false")) multiplexer_1 (
    .in0(_1_ID), .in1(_3_ID), .out(multiplexer_1_out), .sel(reg1));
  Multiplexer #(.width(3), .enable("false")) multiplexer_2 (
    .in0(_2_ID), .in1(_3_ID), .out(multiplexer_2_out), .sel(reg2));
  Multiplexer #(.width(3), .enable("false")) multiplexer_3 (.in0(_3_ID), .in1(3'b111), .out(out_14), .sel(reg3));
  Register_file register_file_1 (
    .Write_back(RB), .BusA(bus_a), .r(R0), .r_2(out_7), .r_3(out_8), .r_4(out_9), .RA(multiplexer_1_out),
    .BusB(bus_b), .r_5(out_10), .r_6(out_11), .r_7(out_12), .r_8(out_13), .RB(multiplexer_2_out),
    .RD(out_14), .Clk(RW_MEM), .write_enable(CLK));
  assign bit_extender_1_out = {{15{IMM5_EX[4]}}, IMM5_EX};  // Bit_Extender bit_extender_1
  Bit_Extender #(.out_width(20), .\type ("sign")) bit_extender_2 (.out(bit_extender_2_out));  // open: in
  ID_EX id_ex_1 (
    .MemWriteID(MEM_W), .fun(func_ID), .JRID(JR), .W_ID(reg3), .JID(J), .bus_a_ID(bus_a), .PCP_4_ID(PC_4_ID),
    .IMM_pc(IMM_PC_ID), .B_ID(B), .ALUopID(ALUOP), .RW_ID(RW), .bus_b_ID(bus_b), .IMM_ID(IMM),
    .ALUSrcID(ALU_SRC), .IMM_8({_1, _2, func}), .WB_ID(WB), .MemReadID(MEM_R), .MemWriteEX(MEM_W_EX),
    .fun_2(func_EX), .JREX(JR_EX), .W_EX(reg3_EX), .JEX(J_EX), .bus_a_EX(bus_a_EX), .PCP_4_EX(PC_4_EX),
    .IMM_pc_2(IMM_PC_EX), .B_EX(B_EX), .ALUopEX(ALUOP_EX), .RW_EX(RW_EX), .bus_b_EX(bus_b_EX),
    .IMM_EX(IMM_EX), .ALUSrcEX(ALU_SRC_EX), .IMM_8_2(IMM8_EX), .WB_EX(WB_EX), .MemReadEX(MEM_R_EX),
    .clk(CLK), .clr(in_5), .OP_CODE(OP_CODE_ID), .OP_CODE_2(OP_CODE_EX), .imm_11(IMM_11_ID),
    .imm_11_2(IMM_11_EX), .imm5(IMM5_ID), .imm5_2(IMM5_EX));
  Multiplexer #(.select(2), .width(20), .enable("false")) multiplexer_4 (
    .in0(bit_extender_1_out), .in1(bit_extender_2_out), .in2({20{1'b0}}), .in3({20{1'b0}}),
    .out(multiplexer_4_out), .sel(IMM));
  Adder #(.width(20)) adder_1 (.a(IMM_PC_EX), .b(20'h1), .out(PC_4), .cin(1'b0));  // open: cout
  Adder #(.width(20)) adder_2 (.a(IMM_PC_EX), .b(multiplexer_4_out), .out(adder_2_out), .cin(1'b0));  // open: cout
  assign bit_extender_3_out = {{9{IMM_11_EX[10]}}, IMM_11_EX};  // Bit_Extender bit_extender_3
  Adder #(.width(20)) adder_3 (.a(multiplexer_4_out), .b(bus_a_EX[19:0]), .out(adder_3_out), .cin(1'b0));  // open: cout
  Multiplexer #(.width(32), .enable("false")) multiplexer_5 (
    .in0(bus_b_EX), .in1(immediate_value_1_to_alu), .out(multiplexer_5_out), .sel(ALU_SRC_EX));
  Multiplexer #(.width(20), .enable("false")) multiplexer_6 (
    .in0(PC_4), .in1(adder_2_out), .out(multiplexer_6_out), .sel(B_EX));
  Multiplexer #(.width(20), .enable("false")) multiplexer_7 (
    .in0(multiplexer_6_out), .in1(adder_4_out), .out(multiplexer_7_out), .sel(J_EX));
  Adder #(.width(20)) adder_4 (.a(IMM_PC_EX), .b(bit_extender_3_out), .out(adder_4_out), .cin(1'b0));  // open: cout
  and and_1 (B_EX, B_EX, Zero_flag);
  ALU alu_1 (
    .in_2(bus_a_EX), .in_4(multiplexer_5_out), .out_6(ALU), .branch(Zero_flag), .FUN(func_EX),
    .ALUop(ALUOP_EX), .OPCODE(OP_CODE_EX));
  IMMEDIATE_VALUE immediate_value_1 (
    .IMM_5(IMM5_EX), .IMM_8(IMM8_EX), .TO_ALU(immediate_value_1_to_alu), .SET(SET_EX), .SEL(IMM_EX));
  Multiplexer #(.width(20), .enable("false")) multiplexer_8 (
    .in0(multiplexer_7_out), .in1(adder_3_out), .out(NEXT_PC), .sel(JR_EX));
  EX_MEM ex_mem_1 (
    .clk(CLK), .clr(in_4), .bus_a_ID(bus_a_EX), .bus_a_EX(bus_a_MEM), .IMM(IMM_EX), .IMM_2(IMM_MEM),
    .IMM_PC(IMM_PC_EX), .IMM_PC_2(IMM_PC_MEM), .ALU(ALU), .ALU_2(ALU_MEM), .WB(WB_EX), .WB_2(WB_MEM),
    .RW(RW_EX), .RW_2(RW_MEM), .MEM_R(MEM_R_EX), .MEM_R_2(MEM_R_MEM), .MEM_W(MEM_W_EX), .MEM_W_2(MEM_W_MEM),
    .imm_8(IMM8_EX), .imm_8_2(IMM8_MEM), .imm5(IMM5_EX), .imm5_2(IMM5_MEM), .B(B_EX), .B_2(Br_MEM),
    .BUS_B(bus_b_EX), .BUS_B_2(bus_b_MEM), .imm_11(IMM_11_EX), .imm_11_2(IMM_11_MEM), .SET(SET_EX),
    .SET_2(SET_MEM), .PC_4(PC_4_EX), .PC_4_2(PC_4_MEM));
  Bit_Extender #(.in_width(32), .out_width(20), .\type ("sign")) bit_extender_4 (
    .in(ALU_MEM), .out(bit_extender_4_out));
  RAM #(.addrWidth(20), .dataWidth(32), .bus("separate")) ram_2 (
    .addr(bit_extender_4_out), .din(bus_b_MEM), .data(MEM_RES), .str(MEM_W_MEM), .clk(CLK), .ld(MEM_R_MEM));  // open: sel, clr
  SSET sset_1 (.IMM_8(IMM8_MEM), .ALU_RES(ALU_MEM), .SSET(SSET_OUT));
  assign bit_extender_5_out = {{12{IMM_PC_MEM[19]}}, IMM_PC_MEM};  // Bit_Extender bit_extender_5
  Adder #(.width(32)) adder_5 (.a(bit_extender_5_out), .b(32'h2), .out(JALR_IN), .cin(1'b0));  // open: cout
  MEM_WB mem_wb_1 (
    .WB(WB_MEM), .clk(CLK), .WB_2(MEM_RES), .SSET(SSET_OUT), .SET(SET_MEM), .JALR(JALR_IN), .ALU(ALU_MEM),
    .WB_3(WB_WB), .clr(1'b1), .WB_4(MEM_RES_WB), .SSET_2(SSET_OUT_WB), .SET_2(SET_WB), .JALR_2(JALR_IN_WB),
    .ALU_2(ALU_WB));
  // WRITE_BACK_TO_REG write_back_to_reg_1: pin names not known; wires that end beside it: MEM_RES_WB, ALU_WB, SET_WB, JALR_IN_WB, ALU_WB, WB_WB, RB

  // Other names for the same wires on the sheet: IMM5[4:0] = {_2, func}; IMM8[7:0] = {_1, _2, func};
  //   IMM_11[10:0] = {_3, _1, _2, func}; R1[31:0] = out_7; R2[31:0] = out_8; R3[31:0] = out_9; R4[31:0] = out_10;
  //   R5[31:0] = out_11; R6[31:0] = out_12; R7[31:0] = out_13

  // Notes on the sheet:
  //   IM
  //   IF/ID
  //   JALR
  //   ID/EX
  //   EX/MEM
  //   Data - MEM
  //   MEM/WB
  //   W.BACK
endmodule

module ALU (
  input  [4:0] ALUop,
  input  [31:0] in_2,
  input  [1:0] FUN,
  input  [31:0] in_4,
  input  [4:0] OPCODE,
  output [31:0] out_6,
  output branch
);

  wire and_2_out, and_3_out, and_4_out, and_5_out, and_6_out, and_7_out, comparator_1_eq, comparator_1_lt,
       comparator_3_eq, comparator_4_eq, comparator_5_eq, comparator_6_eq, comparator_7_eq, comparator_8_eq,
       EN, EQZ, GTZ, LTZ, NEZ, or_2_out, or_3_out;
  wire [31:0] ADDI_ADD, ANDI, ANDI_AND, BEQZ, BGEZ, BGTZ, BLEZ, BLTZ, BNEZ, EQVI_EQV, J, multiplexer_1_out,
       ORI_OR, ROR, SEQI, SEQI_SEQ, SLTI, SLTI_SLT, SRL, SUB, XORI_XOR;

  assign ANDI_AND = in_2 & in_4;  // AND_Gate and_1, 32 bits wide
  assign ORI_OR = in_2 | in_4;  // OR_Gate or_1, 32 bits wide
  assign XORI_XOR = in_2 ^ in_4;  // XOR_Gate xor_1, 32 bits wide
  Adder #(.width(32)) adder_1 (.a(in_2), .b(in_4), .out(ADDI_ADD));  // open: cin, cout
  Subtractor #(.width(32)) subtractor_1 (.a(in_2), .b(in_4), .out(SUB));  // open: bin, bout
  Comparator #(.width(32)) comparator_1 (.a(in_2), .b(in_4), .eq(comparator_1_eq), .lt(comparator_1_lt));  // open: gt
  Shifter #(.width(32)) shifter_1 (.in(in_2), .\dist (in_4[4:0]), .out(SRL));
  Shifter #(.width(32), .shift("lr")) shifter_2 (.in(in_2), .\dist (in_4[4:0]), .out(SRL));
  Shifter #(.width(32), .shift("rr")) shifter_3 (.in(in_2), .\dist (in_4[4:0]), .out(ROR));
  Comparator #(.width(32)) comparator_2 (.a(in_2), .b({32{1'b0}}), .gt(GTZ), .eq(EQZ), .lt(LTZ));
  assign EQVI_EQV = ~(in_2 ^ in_4);  // XNOR_Gate xnor_1, 32 bits wide
  assign SEQI_SEQ = {{31{comparator_1_eq}}, comparator_1_eq};  // Bit_Extender bit_extender_1
  assign SLTI_SLT = {{31{comparator_1_lt}}, comparator_1_lt};  // Bit_Extender bit_extender_2
  not not_1 (NEZ, EQZ);
  Comparator #(.width(5)) comparator_3 (.a(ALUop), .b(5'b10100), .eq(comparator_3_eq));  // open: gt, lt
  Comparator #(.width(5)) comparator_4 (.a(ALUop), .b(5'b10101), .eq(comparator_4_eq));  // open: gt, lt
  Comparator #(.width(5)) comparator_5 (.a(ALUop), .b(5'b10110), .eq(comparator_5_eq));  // open: gt, lt
  Comparator #(.width(5)) comparator_6 (.a(ALUop), .b(5'b10111), .eq(comparator_6_eq));  // open: gt, lt
  Comparator #(.width(5)) comparator_7 (.a(ALUop), .b(5'b11000), .eq(comparator_7_eq));  // open: gt, lt
  Comparator #(.width(5)) comparator_8 (.a(ALUop), .b(5'b11001), .eq(comparator_8_eq));  // open: gt, lt
  assign BEQZ = {{31{EQZ}}, EQZ};  // Bit_Extender bit_extender_3
  assign BLTZ = {{31{LTZ}}, LTZ};  // Bit_Extender bit_extender_4
  assign BGTZ = {{31{EQZ}}, EQZ};  // Bit_Extender bit_extender_5
  assign BNEZ = ~BEQZ;  // NOT_Gate not_2, 32 bits wide
  and and_2 (and_2_out, EQZ, comparator_3_eq);
  and and_3 (and_3_out, NEZ, comparator_4_eq);
  and and_4 (and_4_out, LTZ, comparator_5_eq);
  or or_2 (or_2_out, EQZ, GTZ);
  and and_5 (and_5_out, or_2_out, comparator_6_eq);
  and and_6 (and_6_out, GTZ, comparator_7_eq);
  and and_7 (and_7_out, or_3_out, comparator_8_eq);
  or or_3 (or_3_out, EQZ, LTZ);
  assign BGEZ = BEQZ | BLTZ;  // OR_Gate or_4, 32 bits wide
  assign BLEZ = BEQZ | BGTZ;  // OR_Gate or_5, 32 bits wide
  or or_6 (branch, and_2_out, and_3_out, and_4_out, and_5_out, and_6_out, and_7_out);
  Multiplexer #(.select(3), .width(32)) multiplexer_1 (
    .in0(ANDI_AND), .in1(ORI_OR), .in2(XORI_XOR), .in3(EQVI_EQV), .in4(ADDI_ADD), .in5(SUB), .in6(SLTI),
    .in7(SEQI), .out(multiplexer_1_out), .sel({OPCODE[0], FUN}), .en(EN));
  Multiplexer #(.select(5), .width(32), .enable("false")) multiplexer_2 (
    .in0(multiplexer_1_out), .in1(multiplexer_1_out), .in2({32{1'b0}}), .in3({32{1'b0}}), .in4({32{1'b0}}),
    .in5({32{1'b0}}), .in6(ANDI), .in7(ORI_OR), .in8(XORI_XOR), .in9(EQVI_EQV), .in10(ADDI_ADD), .in11(SLTI),
    .in12(SEQI), .in13(SRL), .in14(SRL), .in15(ROR), .in16(ADDI_ADD), .in17(ADDI_ADD), .in18(ADDI_ADD),
    .in19({32{1'b0}}), .in20({32{1'b0}}), .in21(BEQZ), .in22(BNEZ), .in23(BLTZ), .in24(BGEZ), .in25(BGEZ),
    .in26(BLEZ), .in27({32{1'b0}}), .in28({32{1'b0}}), .in29(ADDI_ADD), .in30(J), .in31({32{1'b0}}),
    .out(out_6), .sel(ALUop));
  nand nand_1 (EN, OPCODE[1], OPCODE[2], OPCODE[3], OPCODE[4]);

  // Other names for the same wires on the sheet: A[31:0] = in_2; ALU_OP[4:0] = ALUop; B[31:0] = in_4;
  //   SHIFT[4:0] = in_4[4:0]; BEQ[31:0] = ADDI_ADD; func[1:0] = FUN; SELE[2:0] = {OPCODE[0], FUN}

  // Notes on the sheet:
  //   ALU OUTPUT
endmodule

// REG
module Register_file (
  input  [31:0] Write_back,
  input  [2:0] RA,
  input  [2:0] RB,
  input  [2:0] RD,
  input  Clk,
  input  write_enable,
  output [31:0] BusA,
  output [31:0] r,
  output [31:0] r_2,
  output [31:0] r_3,
  output [31:0] r_4,
  output [31:0] BusB,
  output [31:0] r_5,
  output [31:0] r_6,
  output [31:0] r_7,
  output [31:0] r_8
);

  wire and_1_out, and_2_out, and_3_out, and_4_out, and_5_out, and_6_out, and_7_out, and_8_out,
       decoder_1_out0, decoder_1_out1, decoder_1_out2, decoder_1_out3, decoder_1_out4, decoder_1_out5,
       decoder_1_out6, decoder_1_out7;

  Decoder #(.select(3)) decoder_1 (
    .out0(decoder_1_out0), .out1(decoder_1_out1), .out2(decoder_1_out2), .out3(decoder_1_out3),
    .out4(decoder_1_out4), .out5(decoder_1_out5), .out6(decoder_1_out6), .out7(decoder_1_out7), .sel(RD),
    .en(1'b1));
  and and_1 (and_1_out, write_enable, decoder_1_out0);
  and and_2 (and_2_out, write_enable, decoder_1_out1);
  and and_3 (and_3_out, write_enable, decoder_1_out2);
  and and_4 (and_4_out, write_enable, decoder_1_out3);
  and and_5 (and_5_out, write_enable, decoder_1_out4);
  and and_6 (and_6_out, write_enable, decoder_1_out5);
  and and_7 (and_7_out, write_enable, decoder_1_out6);
  and and_8 (and_8_out, write_enable, decoder_1_out7);
  Register #(.width(32)) register_1 (.D(Write_back), .en(and_1_out), .Q(r), .clk(Clk));  // open: clr
  Register #(.width(32)) register_2 (.D(Write_back), .en(and_2_out), .Q(r_5), .clk(Clk));  // open: clr
  Register #(.width(32)) register_3 (.D(Write_back), .en(and_3_out), .Q(r_2), .clk(Clk));  // open: clr
  Register #(.width(32)) register_4 (.D(Write_back), .en(and_4_out), .Q(r_6), .clk(Clk));  // open: clr
  Register #(.width(32)) register_5 (.D(Write_back), .en(and_5_out), .Q(r_3), .clk(Clk));  // open: clr
  Register #(.width(32)) register_6 (.D(Write_back), .en(and_6_out), .Q(r_7), .clk(Clk));  // open: clr
  Register #(.width(32)) register_7 (.D(Write_back), .en(and_7_out), .Q(r_4), .clk(Clk));  // open: clr
  Register #(.width(32)) register_8 (.D(Write_back), .en(and_8_out), .Q(r_8), .clk(Clk));  // open: clr
  Multiplexer #(.select(3), .width(32), .enable("false")) multiplexer_1 (
    .in0(r), .in1(r_5), .in2(r_2), .in3(r_6), .in4(r_3), .in5(r_7), .in6(r_4), .in7(r_8), .out(BusA), .sel(RA));
  Multiplexer #(.select(3), .width(32), .enable("false")) multiplexer_2 (
    .in0(r), .in1(r_5), .in2(r_2), .in3(r_6), .in4(r_3), .in5(r_7), .in6(r_4), .in7(r_8), .out(BusB), .sel(RB));

  // Other names for the same wires on the sheet: R0[31:0] = r; R1[31:0] = r_5; R2[31:0] = r_2; R3[31:0] = r_6;
  //   R4[31:0] = r_3; R5[31:0] = r_7; R6[31:0] = r_4; R7[31:0] = r_8
endmodule

module PC (
  input  [19:0] IMMEDIATE_PC,
  input  B,
  input  J,
  input  [4:0] IMM_5,
  input  JR,
  input  [7:0] IMM_8,
  input  [1:0] Imm,
  input  [10:0] IMM_11,
  input  [31:0] Rd,
  output [19:0] PC_IN
);

  wire [19:0] adder_1_out, adder_2_out, adder_3_out, adder_4_out, bit_extender_1_out, bit_extender_2_out,
       bit_extender_3_out, multiplexer_1_out, multiplexer_2_out, multiplexer_3_out;

  assign bit_extender_1_out = {{15{IMM_5[4]}}, IMM_5};  // Bit_Extender bit_extender_1
  Multiplexer #(.select(2), .width(20), .enable("false")) multiplexer_1 (
    .in0(bit_extender_1_out), .in1(bit_extender_2_out), .out(multiplexer_1_out), .sel(Imm));  // open: in2, in3
  assign bit_extender_2_out = {{12{IMM_8[7]}}, IMM_8};  // Bit_Extender bit_extender_2
  Adder #(.width(20)) adder_1 (.a(IMMEDIATE_PC), .b(20'h1), .out(adder_1_out), .cin(1'b0));  // open: cout
  Adder #(.width(20)) adder_2 (.a(IMMEDIATE_PC), .b(multiplexer_1_out), .out(adder_2_out), .cin(1'b0));  // open: cout
  assign bit_extender_3_out = {{9{IMM_11[10]}}, IMM_11};  // Bit_Extender bit_extender_3
  Multiplexer #(.width(20), .enable("false")) multiplexer_2 (
    .in0(adder_1_out), .in1(adder_2_out), .out(multiplexer_2_out), .sel(B));
  Adder #(.width(20)) adder_3 (.a(IMMEDIATE_PC), .b(bit_extender_3_out), .out(adder_3_out), .cin(1'b0));  // open: cout
  Adder #(.width(20)) adder_4 (.a(multiplexer_1_out), .b(Rd[19:0]), .out(adder_4_out), .cin(1'b0));  // open: cout
  Multiplexer #(.width(20), .enable("false")) multiplexer_3 (
    .in0(multiplexer_2_out), .in1(adder_3_out), .out(multiplexer_3_out), .sel(J));
  Multiplexer #(.width(20), .enable("false")) multiplexer_4 (
    .in0(multiplexer_3_out), .in1(adder_4_out), .out(PC_IN), .sel(JR));

  // Other names for the same wires on the sheet: _5[4:0] = IMM_5; _8[7:0] = IMM_8; _11[10:0] = IMM_11;
  //   _20[19:0] = IMMEDIATE_PC
endmodule

module control_unit (
  input  [4:0] Opcode,
  output [4:0] ALUop,
  output ALU_SRC,
  output JR,
  output J,
  output B,
  output MEM_W,
  output MEM_R,
  output RW,
  output [3:0] WB,
  output [1:0] IMM,
  output W,
  output R2,
  output R1
);

  Multiplexer #(.select(5), .width(21), .enable("false")) multiplexer_1 (
    .in0(21'ha00), .in1(21'ha01), .in2({21{1'b0}}), .in3({21{1'b0}}), .in4(21'ha26), .in5(21'ha27),
    .in6(21'ha28), .in7(21'ha29), .in8(21'ha2a), .in9(21'ha2b), .in10(21'ha2c), .in11(21'ha2d),
    .in12(21'ha2e), .in13(21'ha2f), .in14(21'h80310), .in15(21'h80311), .in16(21'h18c32), .in17(21'h90233),
    .in18({21{1'b0}}), .in19({21{1'b0}}), .in20(21'h120214), .in21(21'h120215), .in22(21'h120216),
    .in23(21'h120217), .in24(21'h120218), .in25(21'h120219), .in26(21'h13005a), .in27(21'h7485b),
    .in28(21'h3283c), .in29(21'h12183d), .in30(21'h9e), .in31(21'h14009f),
    .out({R1, R2, W, IMM, WB, RW, MEM_R, MEM_W, B, J, JR, ALU_SRC, ALUop}), .sel(Opcode));
endmodule

module IMMEDIATE_VALUE (
  input  [4:0] IMM_5,
  input  [7:0] IMM_8,
  input  [1:0] SEL,
  output [31:0] TO_ALU,
  output [31:0] SET
);

  wire [31:0] bit_extender_1_out, bit_extender_2_out, bit_extender_3_out;

  assign bit_extender_1_out = {{27{1'b0}}, IMM_5};  // Bit_Extender bit_extender_1
  assign bit_extender_2_out = {{27{IMM_5[4]}}, IMM_5};  // Bit_Extender bit_extender_2
  assign bit_extender_3_out = {{24{1'b0}}, IMM_8};  // Bit_Extender bit_extender_3
  assign SET = {{24{IMM_8[7]}}, IMM_8};  // Bit_Extender bit_extender_4
  Multiplexer #(.select(2), .width(32)) multiplexer_1 (
    .in0(bit_extender_1_out), .in1(bit_extender_2_out), .in2(bit_extender_3_out), .in3(SET), .out(TO_ALU),
    .sel(SEL), .en(1'b1));
endmodule

module SSET (
  input  [7:0] IMM_8,
  input  [31:0] ALU_RES,
  output [31:0] SSET
);


  assign SSET = {ALU_RES[31:8], IMM_8};
endmodule

module WRITE_BACK_TO_REG (
  input  [31:0] MEM,
  input  [31:0] ALU,
  input  [31:0] SSET,
  input  [31:0] SET,
  input  [3:0] WB,
  input  [31:0] JALR,
  output [31:0] back_to_reg
);

  Multiplexer #(.select(4), .width(32)) multiplexer_1 (
    .in0(ALU), .in1(SSET), .in2(SET), .in3({32{1'b0}}), .in4(JALR), .in5({32{1'b0}}), .in6({32{1'b0}}),
    .in7({32{1'b0}}), .in8(MEM), .in9({32{1'b0}}), .in10({32{1'b0}}), .in11({32{1'b0}}), .in12({32{1'b0}}),
    .in13({32{1'b0}}), .in14({32{1'b0}}), .in15({32{1'b0}}), .out(back_to_reg), .sel(WB), .en(1'b1));
endmodule

module EX_MEM (
  input  clk,
  input  clr,
  input  [1:0] IMM,
  input  [31:0] ALU,
  input  [3:0] WB,
  input  RW,
  input  [31:0] BUS_B,
  input  MEM_R,
  input  [19:0] IMM_PC,
  input  MEM_W,
  input  [7:0] imm_8,
  input  [31:0] bus_a_ID,
  input  [31:0] SET,
  input  [10:0] imm_11,
  input  [19:0] PC_4,
  input  [4:0] imm5,
  input  B,
  output [1:0] IMM_2,
  output [31:0] ALU_2,
  output [3:0] WB_2,
  output RW_2,
  output [31:0] BUS_B_2,
  output MEM_R_2,
  output [19:0] IMM_PC_2,
  output MEM_W_2,
  output [7:0] imm_8_2,
  output [31:0] bus_a_EX,
  output [31:0] SET_2,
  output [10:0] imm_11_2,
  output [19:0] PC_4_2,
  output [4:0] imm5_2,
  output B_2
);

  Register #(.width(2)) u_IMM (.D(IMM), .en(1'b1), .Q(IMM_2), .clk(clk), .clr(clr));
  Register #(.width(4)) u_WB (.D(WB), .en(1'b1), .Q(WB_2), .clk(clk), .clr(clr));
  Register #(.width(32)) u_BUS_B (.D(BUS_B), .en(1'b1), .Q(BUS_B_2), .clk(clk), .clr(clr));
  Register #(.width(20)) u_IMM_PC (.D(IMM_PC), .en(1'b1), .Q(IMM_PC_2), .clk(clk), .clr(clr));
  Register register_1 (.D(imm_8), .en(1'b1), .Q(imm_8_2), .clk(clk), .clr(clr));
  Register #(.width(32)) u_SET (.D(SET), .en(1'b1), .Q(SET_2), .clk(clk), .clr(clr));
  Register #(.width(5)) u_imm5 (.D(imm5), .en(1'b1), .Q(imm5_2), .clk(clk), .clr(clr));
  Register #(.width(1)) u_B (.D(B), .en(1'b1), .Q(B_2), .clk(clk), .clr(clr));
  Register #(.width(32)) u_ALU (.D(ALU), .en(1'b1), .Q(ALU_2), .clk(clk), .clr(clr));
  Register #(.width(1)) u_RW (.D(RW), .en(1'b1), .Q(RW_2), .clk(clk), .clr(clr));
  Register #(.width(1)) u_MEM_R (.D(MEM_R), .en(1'b1), .Q(MEM_R_2), .clk(clk), .clr(clr));
  Register #(.width(1)) register_2 (.D(MEM_W), .en(1'b1), .Q(MEM_W_2), .clk(clk), .clr(clr));
  Register #(.width(32)) register_3 (.D(bus_a_ID), .Q(bus_a_EX), .clk(clk), .clr(clr));  // open: en
  Register #(.width(11)) u_imm_11 (.D(imm_11), .en(1'b1), .Q(imm_11_2), .clk(clk), .clr(clr));
  Register #(.width(20)) u_PC_4 (.D(PC_4), .en(1'b1), .Q(PC_4_2), .clk(clk), .clr(clr));
endmodule

module ID_EX (
  input  clk,
  input  clr,
  input  MemWriteID,
  input  [1:0] fun,
  input  JRID,
  input  W_ID,
  input  JID,
  input  [31:0] bus_a_ID,
  input  [19:0] PCP_4_ID,
  input  [19:0] IMM_pc,
  input  B_ID,
  input  [4:0] ALUopID,
  input  RW_ID,
  input  [31:0] bus_b_ID,
  input  [1:0] IMM_ID,
  input  ALUSrcID,
  input  [7:0] IMM_8,
  input  [3:0] WB_ID,
  input  [4:0] OP_CODE,
  input  MemReadID,
  input  [10:0] imm_11,
  input  [4:0] imm5,
  output MemWriteEX,
  output [1:0] fun_2,
  output JREX,
  output W_EX,
  output JEX,
  output [31:0] bus_a_EX,
  output [19:0] PCP_4_EX,
  output [19:0] IMM_pc_2,
  output B_EX,
  output [4:0] ALUopEX,
  output RW_EX,
  output [31:0] bus_b_EX,
  output [1:0] IMM_EX,
  output ALUSrcEX,
  output [7:0] IMM_8_2,
  output [3:0] WB_EX,
  output [4:0] OP_CODE_2,
  output MemReadEX,
  output [10:0] imm_11_2,
  output [4:0] imm5_2
);

  Register #(.width(2)) u_fun (.D(fun), .en(1'b1), .Q(fun_2), .clk(clk), .clr(clr));
  Register #(.width(32)) register_1 (.D(bus_a_ID), .en(1'b1), .Q(bus_a_EX), .clk(clk), .clr(clr));
  Register #(.width(32)) register_2 (.D(bus_b_ID), .en(1'b1), .Q(bus_b_EX), .clk(clk), .clr(clr));
  Register register_3 (.D(IMM_8), .en(1'b1), .Q(IMM_8_2), .clk(clk), .clr(clr));
  Register #(.width(5)) u_OP_CODE (.D(OP_CODE), .en(1'b1), .Q(OP_CODE_2), .clk(clk), .clr(clr));
  Register #(.width(11)) u_imm_11 (.D(imm_11), .en(1'b1), .Q(imm_11_2), .clk(clk), .clr(clr));
  Register #(.width(5)) u_imm5 (.D(imm5), .en(1'b1), .Q(imm5_2), .clk(clk), .clr(clr));
  Register #(.width(20)) register_4 (.D(PCP_4_ID), .en(1'b1), .Q(PCP_4_EX), .clk(clk), .clr(clr));
  Register #(.width(20)) u_IMM_pc (.D(IMM_pc), .en(1'b1), .Q(IMM_pc_2), .clk(clk), .clr(clr));
  Register #(.width(1)) register_5 (.D(JRID), .en(1'b1), .Q(JREX), .clk(clk), .clr(clr));
  Register #(.width(1)) register_6 (.D(JID), .en(1'b1), .Q(JEX), .clk(clk), .clr(clr));
  Register #(.width(1)) register_7 (.D(B_ID), .en(1'b1), .Q(B_EX), .clk(clk), .clr(clr));
  Register #(.width(1)) register_8 (.D(RW_ID), .en(1'b1), .Q(RW_EX), .clk(clk), .clr(clr));
  Register #(.width(2)) register_9 (.D(IMM_ID), .en(1'b1), .Q(IMM_EX), .clk(clk), .clr(clr));
  Register #(.width(1)) register_10 (.D(ALUSrcID), .en(1'b1), .Q(ALUSrcEX), .clk(clk), .clr(clr));
  Register #(.width(4)) register_11 (.D(WB_ID), .en(1'b1), .Q(WB_EX), .clk(clk), .clr(clr));
  Register #(.width(1)) register_12 (.D(MemReadID), .en(1'b1), .Q(MemReadEX), .clk(clk), .clr(clr));
  Register #(.width(1)) register_13 (.D(MemWriteID), .en(1'b1), .Q(MemWriteEX), .clk(clk), .clr(clr));
  Register #(.width(1)) register_14 (.D(W_ID), .en(1'b1), .Q(W_EX), .clk(clk), .clr(clr));
  Register #(.width(5)) register_15 (.D(ALUopID), .en(1'b1), .Q(ALUopEX), .clk(clk), .clr(clr));
endmodule

module IF_ID (
  input  clk,
  input  clr,
  input  [19:0] IMM_PC,
  input  [19:0] IMM_pc___4,
  input  [2:0] _1,
  input  [2:0] _2,
  input  [2:0] _3,
  input  reg_1,
  input  reg_2,
  input  reg_3,
  input  [4:0] WB,
  input  [10:0] imm_11,
  input  [7:0] imm_8,
  input  [4:0] imm5,
  input  [1:0] fun,
  output [19:0] IMM_pc_2,
  output [19:0] IMM_pc___4_2,
  output [2:0] _1_2,
  output [2:0] _2_2,
  output [2:0] _3_2,
  output reg_1_2,
  output reg_2_2,
  output reg_3_2,
  output [4:0] WB_2,
  output [10:0] imm_11_2,
  output [7:0] imm_8_2,
  output [4:0] imm5_2,
  output [1:0] fun_2
);

  Register #(.width(20)) u_IMM_pc (.D(IMM_PC), .en(1'b1), .Q(IMM_pc_2), .clk(clk), .clr(clr));
  Register #(.width(20)) u_IMM_pc___4 (.D(IMM_pc___4), .en(1'b1), .Q(IMM_pc___4_2), .clk(clk), .clr(clr));
  Register #(.width(3)) u__1 (.D(_1), .en(1'b1), .Q(_1_2), .clk(clk), .clr(clr));
  Register #(.width(3)) u__2 (.D(_2), .en(1'b1), .Q(_2_2), .clk(clk), .clr(clr));
  Register #(.width(3)) u__3 (.D(_3), .en(1'b1), .Q(_3_2), .clk(clk), .clr(clr));
  Register #(.width(1)) u_reg_1 (.D(reg_1), .en(1'b1), .Q(reg_1_2), .clk(clk), .clr(clr));
  Register #(.width(1)) u_reg_2 (.D(reg_2), .en(1'b1), .Q(reg_2_2), .clk(clk), .clr(clr));
  Register #(.width(1)) u_reg_3 (.D(reg_3), .en(1'b1), .Q(reg_3_2), .clk(clk), .clr(clr));
  Register #(.width(5)) u_WB (.D(WB), .en(1'b1), .Q(WB_2), .clk(clk), .clr(clr));
  Register #(.width(11)) u_imm_11 (.D(imm_11), .en(1'b1), .Q(imm_11_2), .clk(clk), .clr(clr));
  Register u_imm_8 (.D(imm_8), .en(1'b1), .Q(imm_8_2), .clk(clk), .clr(clr));
  Register #(.width(5)) u_imm5 (.D(imm5), .en(1'b1), .Q(imm5_2), .clk(clk), .clr(clr));
  Register #(.width(2)) u_fun (.D(fun), .en(1'b1), .Q(fun_2), .clk(clk), .clr(clr));

  // Notes on the sheet:
  //   If/ID
endmodule

module MEM_WB (
  input  [3:0] WB,
  input  clk,
  input  clr,
  input  [31:0] WB_2,
  input  [31:0] SSET,
  input  [31:0] SET,
  input  [31:0] JALR,
  input  [31:0] ALU,
  output [3:0] WB_3,
  output [31:0] WB_4,
  output [31:0] SSET_2,
  output [31:0] SET_2,
  output [31:0] JALR_2,
  output [31:0] ALU_2
);

  Register #(.width(4)) IMM (.D(WB), .en(1'b1), .Q(WB_3), .clk(clk), .clr(clr));
  Register #(.width(32)) u_WB (.D(WB_2), .en(1'b1), .Q(WB_4), .clk(clk), .clr(clr));
  Register #(.width(32)) u_SSET (.D(SSET), .en(1'b1), .Q(SSET_2), .clk(clk), .clr(clr));
  Register #(.width(32)) u_SET (.D(SET), .en(1'b1), .Q(SET_2), .clk(clk), .clr(clr));
  Register #(.width(32)) u_JALR (.D(JALR), .en(1'b1), .Q(JALR_2), .clk(clk), .clr(clr));
  Register #(.width(32)) u_ALU (.D(ALU), .en(1'b1), .Q(ALU_2), .clk(clk), .clr(clr));
endmodule

module Hazard_dete (
  input  Read,
  input  RegWrite,
  input  [4:0] WriteReg,
  input  [4:0] Register_num,
  output Hazard
);

  wire comparator_1_eq, comparator_2_eq, not_1_out;

  Comparator #(.width(5)) comparator_1 (.a({5{1'b0}}), .b(WriteReg), .eq(comparator_1_eq));  // open: gt, lt
  Comparator #(.width(5)) comparator_2 (.a(WriteReg), .b(Register_num), .eq(comparator_2_eq));  // open: gt, lt
  not not_1 (not_1_out, comparator_1_eq);
  and and_1 (Hazard, Read, RegWrite, not_1_out, comparator_2_eq);
endmodule

module HAZARD_UNIT (
  input  clk,
  input  ReadRs,
  input  RegWriteMEM,
  input  IsToBranchOrJump,
  input  ReadRt,
  input  [4:0] RS,
  input  RegWriteEX,
  input  [4:0] WriteReg_MEM,
  input  [4:0] WriteReg_EX,
  input  [4:0] RT,
  input  IsLW,
  output FlushIF,
  output [1:0] RsOutput,
  output FlushID,
  output StallIF,
  output StallID,
  output [31:0] BubbleNum,
  output [1:0] RtOutput
);

  wire d_ff_1_q, d_ff_2_q, hazard_dete_1_p5, hazard_dete_2_p5, hazard_dete_3_p5, hazard_dete_4_p5, or_1_out;
  wire [1:0] multiplexer_1_out, multiplexer_2_out;

  // Hazard_dete hazard_dete_1: pin names not known; wires that end beside it: WriteReg_MEM, RS, ReadRs, RegWriteMEM, hazard_dete_1_p5
  // Hazard_dete hazard_dete_2: pin names not known; wires that end beside it: WriteReg_EX, RS, ReadRs, RegWriteEX, hazard_dete_2_p5
  // Hazard_dete hazard_dete_3: pin names not known; wires that end beside it: WriteReg_MEM, RT, ReadRt, RegWriteMEM, hazard_dete_3_p5
  // Hazard_dete hazard_dete_4: pin names not known; wires that end beside it: WriteReg_EX, RT, ReadRt, RegWriteEX, hazard_dete_4_p5
  Multiplexer #(.width(2), .enable("false")) multiplexer_1 (
    .in0(2'b00), .in1(2'b10), .out(multiplexer_1_out), .sel(hazard_dete_1_p5));
  Multiplexer #(.width(2), .enable("false")) multiplexer_2 (
    .in0(2'b00), .in1(2'b10), .out(multiplexer_2_out), .sel(hazard_dete_3_p5));
  Multiplexer #(.width(2), .enable("false")) multiplexer_3 (
    .in0(multiplexer_1_out), .in1(2'b01), .out(RsOutput), .sel(hazard_dete_2_p5));
  Multiplexer #(.width(2), .enable("false")) multiplexer_4 (
    .in0(multiplexer_2_out), .in1(2'b01), .out(RtOutput), .sel(hazard_dete_4_p5));
  or or_1 (or_1_out, hazard_dete_2_p5, hazard_dete_4_p5);
  and and_1 (StallID, IsLW, or_1_out);
  D_Flip_Flop #(.trigger("falling")) d_ff_1 (
    .clk(clk), .D(IsToBranchOrJump), .Q(d_ff_1_q));  // open: Qn, preset, en, reset
  D_Flip_Flop #(.trigger("falling")) d_ff_2 (.clk(clk), .D(StallID), .Q(d_ff_2_q));  // open: Qn, preset, en, reset
  Counter #(.width(32), .max('hffffffff)) counter_1 (
    .count(StallID), .Q(BubbleNum), .clk(clk));  // open: load, D, carry, clr
  and and_2 (FlushIF, ~clk, d_ff_1_q);  // AND_Gate
  and and_3 (FlushID, clk, d_ff_2_q);

  assign StallIF = StallID;

  // Other names for the same wires on the sheet: ReadWriteEX = RegWriteEX; ReadWriteMEM = RegWriteMEM

  // Notes on the sheet:
  //   Rs Hazard in MEM
  //   Rs Hazard in EX
  //   Rt Hazard in MEM
  //   Rt Hazard in EX
  //   hasHazard
endmodule

module Forwarding_unit (
  input  [3:0] RA,
  input  [3:0] RDP,
  input  [3:0] RDPP,
  input  [3:0] RDPPP,
  input  [3:0] RB,
  output [1:0] A1A0,
  output [1:0] B1B0
);

  wire and_3_out, and_6_out, comparator_1_eq, comparator_2_eq, comparator_3_eq, comparator_4_eq,
       comparator_5_eq, comparator_6_eq, comparator_7_eq, comparator_8_eq;
  wire [1:0] and_1_out, and_4_out;

  Comparator #(.width(4)) comparator_1 (.a(4'b0000), .b(RA), .eq(comparator_1_eq));  // open: gt, lt
  Comparator #(.width(4)) comparator_2 (.a(RA), .b(RDP), .eq(comparator_2_eq));  // open: gt, lt
  Comparator #(.width(4)) comparator_3 (.a(RA), .b(RDPP), .eq(comparator_3_eq));  // open: gt, lt
  Comparator #(.width(4)) comparator_4 (.a(RB), .b(4'b0000), .eq(comparator_4_eq));  // open: gt, lt
  Comparator #(.width(4)) comparator_5 (.a(RB), .b(RDP), .eq(comparator_5_eq));  // open: gt, lt
  Comparator #(.width(4)) comparator_6 (.a(RB), .b(RDPP), .eq(comparator_6_eq));  // open: gt, lt
  Comparator #(.width(4)) comparator_7 (.a(RA), .b(RDPPP), .eq(comparator_7_eq));  // open: gt, lt
  Comparator #(.width(4)) comparator_8 (.a(RB), .b(RDPPP), .eq(comparator_8_eq));  // open: gt, lt
  and and_1 (and_1_out[0], ~comparator_4_eq, comparator_5_eq);  // AND_Gate
  and and_2 (and_1_out[1], ~comparator_4_eq, ~comparator_5_eq, comparator_6_eq);  // AND_Gate
  and and_3 (and_3_out, ~comparator_4_eq, ~comparator_5_eq, ~comparator_6_eq, comparator_8_eq);  // AND_Gate
  and and_4 (and_4_out[0], ~comparator_1_eq, comparator_2_eq);  // AND_Gate
  and and_5 (and_4_out[1], ~comparator_1_eq, ~comparator_2_eq, comparator_3_eq);  // AND_Gate
  and and_6 (and_6_out, ~comparator_1_eq, ~comparator_2_eq, ~comparator_3_eq, comparator_7_eq);  // AND_Gate
  Multiplexer #(.width(2), .enable("false")) multiplexer_1 (.in0(and_4_out), .in1(2'b11), .out(A1A0), .sel(and_6_out));
  Multiplexer #(.width(2), .enable("false")) multiplexer_2 (.in0(and_1_out), .in1(2'b11), .out(B1B0), .sel(and_3_out));

  // Notes on the sheet:
  //   EX
  //   Mem
endmodule

module Single_cycle (
  input  in_1,
  input  in_2,
  output [31:0] R0,
  output [31:0] out_4,
  output [31:0] out_5,
  output [31:0] out_6,
  output [31:0] out_7,
  output [31:0] out_8,
  output [31:0] out_9,
  output [31:0] out_10,
  output [15:0] out_11,
  output [2:0] out_12,
  output [31:0] out_13,
  output [31:0] out_14,
  output [31:0] out_15,
  output [4:0] out_16,
  output [4:0] out_17,
  output [7:0] out_18
);

  wire ALU_SRC, B, BR, CLK, J, JR, MEM_R, MEM_W, reg1, reg2, reg3, RW, Zero_flag;
  wire [1:0] IMM;
  wire [2:0] multiplexer_1_out, multiplexer_2_out;
  wire [3:0] WB;
  wire [4:0] ALUOP;
  wire [19:0] adder_2_out, adder_3_out, adder_4_out, bit_extender_1_out, bit_extender_2_out,
       bit_extender_3_out, bit_extender_4_out, IMM_PC, multiplexer_5_out, multiplexer_6_out,
       multiplexer_7_out, NEXT_PC, PC_4;
  wire [31:0] ALU_IN, bit_extender_5_out, bus_b, JALR, MEM, multiplexer_4_out, SET, SSET;

  Clock u_CLK (.out(CLK));
  Register #(.width(20)) PC (.D(NEXT_PC), .en(1'b1), .Q(IMM_PC), .clk(CLK), .clr(in_1));
  RAM #(.addrWidth(20), .dataWidth(16)) ram_1 (
    .addr(IMM_PC), .data(out_11), .sel(1'b1), .clk(CLK), .ld(1'b1), .clr(in_2));
  control_unit control_unit_1 (
    .ALUop(ALUOP), .ALU_SRC(ALU_SRC), .JR(JR), .J(J), .B(B), .MEM_W(MEM_W), .MEM_R(MEM_R), .RW(RW), .WB(WB),
    .IMM(IMM), .W(reg3), .Opcode(out_11[15:11]), .R2(reg2), .R1(reg1));
  Multiplexer #(.width(3), .enable("false")) multiplexer_1 (
    .in0(out_11[7:5]), .in1(out_11[10:8]), .out(multiplexer_1_out), .sel(reg1));
  Multiplexer #(.width(3), .enable("false")) multiplexer_2 (
    .in0(out_11[4:2]), .in1(out_11[10:8]), .out(multiplexer_2_out), .sel(reg2));
  Multiplexer #(.width(3), .enable("false")) multiplexer_3 (.in0(out_11[10:8]), .in1(3'b111), .out(out_12), .sel(reg3));
  Register_file register_file_1 (
    .Write_back(out_14), .BusA(out_13), .r(R0), .r_2(out_4), .r_3(out_5), .r_4(out_6),
    .RA(multiplexer_1_out), .BusB(bus_b), .r_5(out_7), .r_6(out_8), .r_7(out_9), .r_8(out_10),
    .RB(multiplexer_2_out), .RD(out_12), .Clk(RW), .write_enable(CLK));
  Multiplexer #(.width(32), .enable("false")) multiplexer_4 (
    .in0(bus_b), .in1(ALU_IN), .out(multiplexer_4_out), .sel(ALU_SRC));
  assign bit_extender_1_out = {{15{out_11[4]}}, out_11[4:0]};  // Bit_Extender bit_extender_1
  Bit_Extender #(.out_width(20), .\type ("sign")) bit_extender_2 (.out(bit_extender_2_out));  // open: in
  and and_1 (BR, B, Zero_flag);
  // ALU alu_1: pin names not known; wires that end beside it: out_13, multiplexer_4_out, out_11[1:0], Zero_flag, out_11[15:11], ALUOP, out_15
  IMMEDIATE_VALUE immediate_value_1 (.IMM_5(out_11[4:0]), .IMM_8(out_11[7:0]), .TO_ALU(ALU_IN), .SET(SET), .SEL(IMM));
  Multiplexer #(.select(2), .width(20), .enable("false")) multiplexer_5 (
    .in0(bit_extender_1_out), .in1(bit_extender_2_out), .in2({20{1'b0}}), .in3({20{1'b0}}),
    .out(multiplexer_5_out), .sel(IMM));
  Bit_Extender #(.in_width(32), .out_width(20), .\type ("sign")) bit_extender_3 (.in(out_15), .out(bit_extender_3_out));
  Adder #(.width(20)) adder_1 (.a(IMM_PC), .b(20'h1), .out(PC_4), .cin(1'b0));  // open: cout
  Adder #(.width(20)) adder_2 (.a(IMM_PC), .b(multiplexer_5_out), .out(adder_2_out), .cin(1'b0));  // open: cout
  assign bit_extender_4_out = {{9{out_11[10]}}, out_11[10:0]};  // Bit_Extender bit_extender_4
  SSET sset_1 (.IMM_8(out_11[7:0]), .ALU_RES(out_15), .SSET(SSET));
  assign bit_extender_5_out = {{12{IMM_PC[19]}}, IMM_PC};  // Bit_Extender bit_extender_5
  Multiplexer #(.width(20), .enable("false")) multiplexer_6 (
    .in0(PC_4), .in1(adder_2_out), .out(multiplexer_6_out), .sel(BR));
  Adder #(.width(20)) adder_3 (.a(IMM_PC), .b(bit_extender_4_out), .out(adder_3_out), .cin(1'b0));  // open: cout
  Adder #(.width(20)) adder_4 (.a(multiplexer_5_out), .b(out_13[19:0]), .out(adder_4_out), .cin(1'b0));  // open: cout
  RAM #(.addrWidth(20), .dataWidth(32), .bus("separate")) ram_2 (
    .addr(bit_extender_3_out), .din(bus_b), .data(MEM), .str(MEM_W), .clk(CLK), .ld(MEM_R));  // open: sel, clr
  Adder #(.width(32)) adder_5 (.a(bit_extender_5_out), .b(32'h2), .out(JALR), .cin(1'b0));  // open: cout
  Multiplexer #(.width(20), .enable("false")) multiplexer_7 (
    .in0(multiplexer_6_out), .in1(adder_3_out), .out(multiplexer_7_out), .sel(J));
  Multiplexer #(.width(20), .enable("false")) multiplexer_8 (
    .in0(multiplexer_7_out), .in1(adder_4_out), .out(NEXT_PC), .sel(JR));
  WRITE_BACK_TO_REG write_back_to_reg_1 (
    .MEM(MEM), .ALU(out_15), .SSET(SSET), .SET(SET), .JALR(JALR), .back_to_reg(out_14), .WB(WB));

  assign out_16 = out_11[15:11];
  assign out_17 = out_11[4:0];
  assign out_18 = out_11[7:0];

  // Other names for the same wires on the sheet: ALU[31:0] = out_15; bus_a[31:0] = out_13; func[1:0] = out_11[1:0];
  //   IMM5[4:0] = out_11[4:0]; IMM8[7:0] = out_11[7:0]; IMM_11[10:0] = out_11[10:0]; _2[2:0] = out_11[4:2];
  //   _1[2:0] = out_11[7:5]; _3[2:0] = out_11[10:8]; OP_CODE[4:0] = out_11[15:11]; R1[31:0] = out_4; R2[31:0] = out_5;
  //   R3[31:0] = out_6; R4[31:0] = out_7; R5[31:0] = out_8; R6[31:0] = out_9; R7[31:0] = out_10; RB[31:0] = out_14

  // Notes on the sheet:
  //   Output Reg
  //   Inst.Memory
  //   IM
  //   JALR
  //   Control unit
  //   Reg.file
  //   ALU
  //   PC
  //   Data - MEM
  //   DM
  //   W. BACK
endmodule
