// Logisim project Sngle Cycle.circ as structural Verilog: 9 circuits, main circuit main
module main (
  input  in_1,
  input  in_2,
  input  in_3,
  output [31:0] R0,
  output [31:0] R0_2,
  output [31:0] R0_3,
  output [19:0] out_7,
  output [4:0] R0_4,
  output [31:0] R0_5,
  output [4:0] R0_6,
  output [31:0] R0_7,
  output [31:0] out_12,
  output [31:0] out_13,
  output [31:0] out_14,
  output [31:0] out_15,
  output [31:0] out_16,
  output [31:0] out_17,
  output [31:0] out_18
);

  wire ALU_SRC, and_1_out, B, BRANCH, CLK, J, JR, MEM_R, MEM_W, reg1, reg2, reg3, RW;
  wire [1:0] IMM;
  wire [2:0] multiplexer_1_out, multiplexer_2_out, multiplexer_3_out;
  wire [3:0] WB;
  wire [4:0] ALUOP, OP_CODE;
  wire [7:5] IMM8;
  wire [10:8] IMM_11;
  wire [19:0] bit_extender_1_out, NEXT_PC;
  wire [31:0] adder_1_out, bit_extender_2_out, immediate_value_1_set, ram_2_data, register_file_1_bus_a,
       register_file_1_bus_b, sset_1_sset;

  Register #(.width(20)) PC (.D(NEXT_PC), .en(1'b1), .Q(out_7), .clk(CLK), .clr(in_1));
  Clock u_CLK (.out(CLK));
  control_unit control_unit_1 (
    .Opcode(OP_CODE), .ALUop(ALUOP), .ALU_SRC(ALU_SRC), .JR(JR), .J(J), .B(B), .MEM_W(MEM_W), .MEM_R(MEM_R),
    .RW(RW), .WB(WB), .IMM(IMM), .W(reg3), .R2(reg2), .R1(reg1));
  RAM #(.addrWidth(20), .dataWidth(16)) ram_1 (
    .addr(out_7), .data({OP_CODE, IMM_11, IMM8, R0_4}), .sel(1'b1), .clk(CLK), .ld(1'b1), .clr(in_3));
  Multiplexer #(.width(3), .enable("false")) multiplexer_1 (
    .in0(IMM8), .in1(IMM_11), .out(multiplexer_1_out), .sel(reg1));
  Multiplexer #(.width(3), .enable("false")) multiplexer_2 (
    .in0(R0_4[4:2]), .in1(IMM_11), .out(multiplexer_2_out), .sel(reg2));
  Multiplexer #(.width(3), .enable("false")) multiplexer_3 (
    .in0(IMM_11), .in1(3'b111), .out(multiplexer_3_out), .sel(reg3));
  Register_file register_file_1 (
    .Rt(multiplexer_1_out), .Rs(multiplexer_2_out), .Rw(multiplexer_3_out), .bus_W(R0_3), .R0(R0_7),
    .out_10(out_12), .out_11(out_13), .out_12(out_14), .out_13(out_15), .out_14(out_16), .out_15(out_17),
    .out_16(out_18), .bus_b(register_file_1_bus_b), .bus_A(register_file_1_bus_a), .read___write(RW),
    .clock(CLK));
  PC pc_2 (
    .IMMEDIATE_PC(out_7), .IMM_11({IMM_11, IMM8, R0_4}), .Rd(out_12), .PC_IN(NEXT_PC), .Imm(IMM),
    .B(and_1_out), .J(J), .JR(JR), .IMM_8({IMM8, R0_4}), .IMM_5(R0_4));
  and and_1 (and_1_out, BRANCH, B);
  Multiplexer #(.width(32), .enable("false")) multiplexer_4 (
    .in0(register_file_1_bus_a), .in1(R0_5), .out(R0_2), .sel(ALU_SRC));
  IMMEDIATE_VALUE immediate_value_1 (
    .IMM_5(R0_4), .IMM_8({IMM8, R0_4}), .TO_ALU(R0_5), .SET(immediate_value_1_set), .SEL(IMM));
  ALU alu_1 (
    .branch(BRANCH), .in_2(R0_2), .in_1(register_file_1_bus_b), .RESULT_2(R0), .FUN(R0_4[1:0]),
    .ALUop(ALUOP), .OPCODE(OP_CODE));  // open: RESULT
  Bit_Extender #(.in_width(32), .out_width(20), .\type ("sign")) bit_extender_1 (.in(R0), .out(bit_extender_1_out));
  assign bit_extender_2_out = {{12{out_7[19]}}, out_7};  // Bit_Extender bit_extender_2
  RAM #(.addrWidth(20), .dataWidth(32), .bus("separate")) ram_2 (
    .addr(bit_extender_1_out), .din(register_file_1_bus_a), .data(ram_2_data), .str(MEM_W), .sel(1'b1),
    .clk(CLK), .ld(MEM_R), .clr(in_2));
  SSET sset_1 (.IMM_8({IMM8, R0_4}), .ALU_RES(R0), .SSET(sset_1_sset));
  WRITE_BACK_TO_REG write_back_to_reg_1 (
    .MEM(ram_2_data), .ALU(R0), .SSET(sset_1_sset), .SET(immediate_value_1_set), .JALR(adder_1_out), .WB(WB),
    .back_to_reg(R0_3));
  Adder #(.width(32)) adder_1 (.a(bit_extender_2_out), .b(32'h2), .out(adder_1_out));  // open: cin, cout

  assign R0_6 = R0_4;

  // Other names for the same wires on the sheet: func[1:0] = R0_4[1:0]; IMM5[4:0] = R0_4; IMM8[4:0] = R0_4;
  //   IMM_11[7:0] = {IMM8, R0_4}; IMM_PC[19:0] = out_7; R0_t[31:0] = R0_7; R1[31:0] = out_12; R2[31:0] = out_13;
  //   R3[31:0] = out_14; R4[31:0] = out_15; R5[31:0] = out_16; R6[31:0] = out_17; R7[31:0] = out_18; RB[31:0] = R0_3

  // Notes on the sheet:
  //   IM
  //   JALR
  //   DM
  //   WRITE BACK
endmodule

module ALU (
  input  [31:0] in_1,
  input  [31:0] in_2,
  input  [1:0] FUN,
  input  [4:0] ALUop,
  input  [4:0] OPCODE,
  output [31:0] RESULT,
  output [31:0] RESULT_2,
  output branch
);

  wire and_2_out, and_3_out, and_4_out, and_5_out, and_6_out, and_7_out, comparator_1_eq, comparator_1_lt,
       comparator_3_eq, comparator_4_eq, comparator_5_eq, comparator_6_eq, comparator_7_eq, comparator_8_eq,
       EN, EQZ, GTZ, LTZ, NEZ, or_2_out, or_3_out;
  wire [31:0] ADDI_ADD, ANDI, ANDI_AND, BEQ, BEQZ, BGEZ, BGTZ, BLEZ, BLTZ, BNE, BNEZ, EQVI_EQV, J,
       mux_3_8_1_out_12, ORI_OR, ROR, SEQI, SEQI_SEQ, SLTI, SLTI_SLT, SRL, SUB, XORI_XOR;

  assign ANDI_AND = in_1 & in_2;  // AND_Gate and_1, 32 bits wide
  assign ORI_OR = in_1 | in_2;  // OR_Gate or_1, 32 bits wide
  assign XORI_XOR = in_1 ^ in_2;  // XOR_Gate xor_1, 32 bits wide
  Adder #(.width(32)) adder_1 (.a(in_1), .b(in_2), .out(ADDI_ADD));  // open: cin, cout
  Subtractor #(.width(32)) subtractor_1 (.a(in_1), .b(in_2), .out(SUB));  // open: bin, bout
  Comparator #(.width(32)) comparator_1 (.a(in_1), .b(in_2), .eq(comparator_1_eq), .lt(comparator_1_lt));  // open: gt
  Shifter #(.width(32)) shifter_1 (.in(in_1), .\dist (in_2[4:0]), .out(SRL));
  Shifter #(.width(32), .shift("lr")) shifter_2 (.in(in_1), .\dist (in_2[4:0]), .out(SRL));
  Shifter #(.width(32), .shift("rr")) shifter_3 (.in(in_1), .\dist (in_2[4:0]), .out(ROR));
  Comparator #(.width(32)) comparator_2 (.a(in_1), .b({32{1'b0}}), .gt(GTZ), .eq(EQZ), .lt(LTZ));
  assign EQVI_EQV = ~(in_1 ^ in_2);  // XNOR_Gate xnor_1, 32 bits wide
  assign SEQI_SEQ = {{31{comparator_1_eq}}, comparator_1_eq};  // Bit_Extender bit_extender_1
  assign SLTI_SLT = {{31{comparator_1_lt}}, comparator_1_lt};  // Bit_Extender bit_extender_2
  not not_1 (NEZ, EQZ);
  Comparator #(.width(5)) comparator_3 (.a(ALUop), .b(5'b10100), .eq(comparator_3_eq));  // open: gt, lt
  Comparator #(.width(5)) comparator_4 (.a(ALUop), .b(5'b10101), .eq(comparator_4_eq));  // open: gt, lt
  Comparator #(.width(5)) comparator_5 (.a(ALUop), .b(5'b10110), .eq(comparator_5_eq));  // open: gt, lt
  Comparator #(.width(5)) comparator_6 (.a(ALUop), .b(5'b10111), .eq(comparator_6_eq));  // open: gt, lt
  Comparator #(.width(5)) comparator_7 (.a(ALUop), .b(5'b11000), .eq(comparator_7_eq));  // open: gt, lt
  Comparator #(.width(5)) comparator_8 (.a(ALUop), .b(5'b11001), .eq(comparator_8_eq));  // open: gt, lt
  assign BEQZ = {{31{EQZ}}, EQZ};  // Bit_Extender bit_extender_3
  assign BLTZ = {{31{LTZ}}, LTZ};  // Bit_Extender bit_extender_4
  assign BGTZ = {{31{EQZ}}, EQZ};  // Bit_Extender bit_extender_5
  nand nand_1 (EN, OPCODE[1], OPCODE[2], OPCODE[3], OPCODE[4]);
  assign BNEZ = ~BEQZ;  // NOT_Gate not_2, 32 bits wide
  and and_2 (and_2_out, EQZ, comparator_3_eq);
  and and_3 (and_3_out, NEZ, comparator_4_eq);
  and and_4 (and_4_out, LTZ, comparator_5_eq);
  or or_2 (or_2_out, EQZ, GTZ);
  and and_5 (and_5_out, or_2_out, comparator_6_eq);
  and and_6 (and_6_out, GTZ, comparator_7_eq);
  and and_7 (and_7_out, or_3_out, comparator_8_eq);
  or or_3 (or_3_out, EQZ, LTZ);
  assign BGEZ = BEQZ | BLTZ;  // OR_Gate or_4, 32 bits wide
  assign BLEZ = BEQZ | BGTZ;  // OR_Gate or_5, 32 bits wide
  or or_6 (branch, and_2_out, and_3_out, and_4_out, and_5_out, and_6_out, and_7_out);
  MUX_3_8 mux_3_8_1 (
    .Data0(ANDI_AND), .Data2(ORI_OR), .Data2_2(XORI_XOR), .Data3(EQVI_EQV), .Data4(ADDI_ADD), .Data5(SUB),
    .Data6(SLTI), .Data7(SEQI), .s2(OPCODE[0]), .s1(FUN[0]), .s0(FUN[1]), .out_12(mux_3_8_1_out_12));
  Multiplexer #(.select(5), .width(32), .enable("false")) multiplexer_1 (
    .in0(mux_3_8_1_out_12), .in1(mux_3_8_1_out_12), .in2({32{1'b0}}), .in3({32{1'b0}}), .in4(ADDI_ADD),
    .in5(ORI_OR), .in6(ANDI), .in7(XORI_XOR), .in8(EQVI_EQV), .in9(SLTI), .in10(SEQI), .in11(SRL),
    .in12(SRL), .in13(ROR), .in14(BEQ), .in15(BNE), .in16(ADDI_ADD), .in17(ADDI_ADD), .in18({32{1'b0}}),
    .in19({32{1'b0}}), .in20(BEQZ), .in21(BNEZ), .in22(BLTZ), .in23(BGEZ), .in24(BGEZ), .in25(BLEZ),
    .in26({32{1'b0}}), .in27({32{1'b0}}), .in28({32{1'b0}}), .in29({32{1'b0}}), .in30(J), .in31({32{1'b0}}),
    .out(RESULT), .sel(ALUop));

  assign RESULT_2 = RESULT;

  // Other names for the same wires on the sheet: A[31:0] = in_1; ALU_OP[4:0] = ALUop; B[31:0] = in_2;
  //   SHIFT[4:0] = in_2[4:0]; func[1:0] = FUN

  // Notes on the sheet:
  //   ALU OUTPUT
  //   ALU INTPUT
endmodule

// REG
module Register_file (
  input  [2:0] Rt,
  input  [2:0] Rs,
  input  [2:0] Rw,
  input  [31:0] bus_W,
  input  read___write,
  input  clock,
  output [31:0] bus_b,
  output [31:0] bus_A,
  output [31:0] R0,
  output [31:0] out_10,
  output [31:0] out_11,
  output [31:0] out_12,
  output [31:0] out_13,
  output [31:0] out_14,
  output [31:0] out_15,
  output [31:0] out_16
);

  wire and_1_out, and_2_out, and_3_out, and_4_out, and_5_out, and_6_out, and_7_out, and_8_out,
       decoder_1_out0, decoder_1_out1, decoder_1_out2, decoder_1_out3, decoder_1_out4, decoder_1_out5,
       decoder_1_out6, decoder_1_out7, decoder_2_out0, decoder_2_out1, decoder_2_out2, decoder_2_out3,
       decoder_2_out4, decoder_2_out5, decoder_2_out6, decoder_2_out7, decoder_3_out0, decoder_3_out1,
       decoder_3_out2, decoder_3_out3, decoder_3_out4, decoder_3_out5, decoder_3_out6, decoder_3_out7;

  Decoder #(.select(3), .disabled(0), .enable("false")) decoder_1 (
    .out0(decoder_1_out0), .out1(decoder_1_out1), .out2(decoder_1_out2), .out3(decoder_1_out3),
    .out4(decoder_1_out4), .out5(decoder_1_out5), .out6(decoder_1_out6), .out7(decoder_1_out7), .sel(Rw));
  and and_1 (and_1_out, decoder_1_out0, read___write);
  and and_2 (and_2_out, decoder_1_out1, read___write);
  and and_3 (and_3_out, decoder_1_out2, read___write);
  and and_4 (and_4_out, decoder_1_out3, read___write);
  and and_5 (and_5_out, decoder_1_out4, read___write);
  and and_6 (and_6_out, decoder_1_out5, read___write);
  and and_7 (and_7_out, decoder_1_out6, read___write);
  and and_8 (and_8_out, decoder_1_out7, read___write);
  Register #(.width(32)) register_1 (.D(bus_W), .en(and_1_out), .Q(R0), .clk(clock));  // open: clr
  Register #(.width(32)) register_2 (.D(bus_W), .en(and_2_out), .Q(out_10), .clk(clock));  // open: clr
  Register #(.width(32)) register_3 (.D(bus_W), .en(and_3_out), .Q(out_11), .clk(clock));  // open: clr
  Register #(.width(32)) register_4 (.D(bus_W), .en(and_4_out), .Q(out_12), .clk(clock));  // open: clr
  Register #(.width(32)) register_5 (.D(bus_W), .en(and_5_out), .Q(out_13), .clk(clock));  // open: clr
  Register #(.width(32)) register_6 (.D(bus_W), .en(and_6_out), .Q(out_14), .clk(clock));  // open: clr
  Register #(.width(32)) register_7 (.D(bus_W), .en(and_7_out), .Q(out_15), .clk(clock));  // open: clr
  Register #(.width(32)) register_8 (.D(bus_W), .en(and_8_out), .Q(out_16), .clk(clock));  // open: clr
  Decoder #(.select(3), .disabled(0), .enable("false")) decoder_2 (
    .out0(decoder_2_out0), .out1(decoder_2_out1), .out2(decoder_2_out2), .out3(decoder_2_out3),
    .out4(decoder_2_out4), .out5(decoder_2_out5), .out6(decoder_2_out6), .out7(decoder_2_out7), .sel(Rs));
  assign bus_A = decoder_2_out0 ? R0 : 32'bz;  // Controlled_Buffer controlled_buffer_1
  assign bus_A = decoder_2_out1 ? out_10 : 32'bz;  // Controlled_Buffer controlled_buffer_2
  assign bus_A = decoder_2_out2 ? out_11 : 32'bz;  // Controlled_Buffer controlled_buffer_3
  assign bus_A = decoder_2_out3 ? out_12 : 32'bz;  // Controlled_Buffer controlled_buffer_4
  assign bus_A = decoder_2_out4 ? out_13 : 32'bz;  // Controlled_Buffer controlled_buffer_5
  assign bus_A = decoder_2_out5 ? out_14 : 32'bz;  // Controlled_Buffer controlled_buffer_6
  assign bus_A = decoder_2_out6 ? out_15 : 32'bz;  // Controlled_Buffer controlled_buffer_7
  assign bus_A = decoder_2_out7 ? out_16 : 32'bz;  // Controlled_Buffer controlled_buffer_8
  Decoder #(.select(3), .disabled(0), .enable("false")) decoder_3 (
    .out0(decoder_3_out0), .out1(decoder_3_out1), .out2(decoder_3_out2), .out3(decoder_3_out3),
    .out4(decoder_3_out4), .out5(decoder_3_out5), .out6(decoder_3_out6), .out7(decoder_3_out7), .sel(Rt));
  assign bus_b = decoder_3_out0 ? R0 : 32'bz;  // Controlled_Buffer controlled_buffer_9
  assign bus_b = decoder_3_out1 ? out_10 : 32'bz;  // Controlled_Buffer controlled_buffer_10
  assign bus_b = decoder_3_out2 ? out_11 : 32'bz;  // Controlled_Buffer controlled_buffer_11
  assign bus_b = decoder_3_out3 ? out_12 : 32'bz;  // Controlled_Buffer controlled_buffer_12
  assign bus_b = decoder_3_out4 ? out_13 : 32'bz;  // Controlled_Buffer controlled_buffer_13
  assign bus_b = decoder_3_out5 ? out_14 : 32'bz;  // Controlled_Buffer controlled_buffer_14
  assign bus_b = decoder_3_out6 ? out_15 : 32'bz;  // Controlled_Buffer controlled_buffer_15
  assign bus_b = decoder_3_out7 ? out_16 : 32'bz;  // Controlled_Buffer controlled_buffer_16

  // Other names for the same wires on the sheet: R1[31:0] = out_10; R2[31:0] = out_11; R3[31:0] = out_12;
  //   R4[31:0] = out_13; R5[31:0] = out_14; R6[31:0] = out_15; R7[31:0] = out_16
endmodule

module PC (
  input  [19:0] IMMEDIATE_PC,
  input  B,
  input  J,
  input  JR,
  input  [4:0] IMM_5,
  input  [7:0] IMM_8,
  input  [10:0] IMM_11,
  input  [1:0] Imm,
  input  [31:0] Rd,
  output [19:0] PC_IN
);

  wire [19:0] adder_1_out, adder_2_out, adder_3_out, adder_4_out, bit_extender_1_out, bit_extender_2_out,
       bit_extender_3_out, multiplexer_1_out, multiplexer_2_out, multiplexer_3_out;

  assign bit_extender_1_out = {{15{IMM_5[4]}}, IMM_5};  // Bit_Extender bit_extender_1
  Multiplexer #(.select(2), .width(20), .enable("false")) multiplexer_1 (
    .in0(bit_extender_1_out), .in1(bit_extender_2_out), .out(multiplexer_1_out), .sel(Imm));  // open: in2, in3
  assign bit_extender_2_out = {{12{IMM_8[7]}}, IMM_8};  // Bit_Extender bit_extender_2
  Adder #(.width(20)) adder_1 (.a(IMMEDIATE_PC), .b(20'h1), .out(adder_1_out), .cin(1'b0));  // open: cout
  Adder #(.width(20)) adder_2 (.a(IMMEDIATE_PC), .b(multiplexer_1_out), .out(adder_2_out), .cin(1'b0));  // open: cout
  assign bit_extender_3_out = {{9{IMM_11[10]}}, IMM_11};  // Bit_Extender bit_extender_3
  Multiplexer #(.width(20), .enable("false")) multiplexer_2 (
    .in0(adder_1_out), .in1(adder_2_out), .out(multiplexer_2_out), .sel(B));
  Adder #(.width(20)) adder_3 (.a(IMMEDIATE_PC), .b(bit_extender_3_out), .out(adder_3_out), .cin(1'b0));  // open: cout
  Adder #(.width(20)) adder_4 (.a(multiplexer_1_out), .b(Rd[19:0]), .out(adder_4_out), .cin(1'b0));  // open: cout
  Multiplexer #(.width(20), .enable("false")) multiplexer_3 (
    .in0(multiplexer_2_out), .in1(adder_3_out), .out(multiplexer_3_out), .sel(J));
  Multiplexer #(.width(20), .enable("false")) multiplexer_4 (
    .in0(multiplexer_3_out), .in1(adder_4_out), .out(PC_IN), .sel(JR));

  // Other names for the same wires on the sheet: _5[4:0] = IMM_5; _8[7:0] = IMM_8; _11[10:0] = IMM_11;
  //   _20[19:0] = IMMEDIATE_PC
endmodule

module control_unit (
  input  [4:0] Opcode,
  output [4:0] ALUop,
  output ALU_SRC,
  output JR,
  output J,
  output B,
  output MEM_W,
  output MEM_R,
  output RW,
  output [3:0] WB,
  output [1:0] IMM,
  output W,
  output R2,
  output R1
);

  wire [20:0] undriven;

  Multiplexer #(.select(5), .width(21), .enable("false")) multiplexer_1 (
    .in0(21'h800), .in1(21'h801), .in2(undriven), .in3(undriven), .in4(21'h826), .in5(21'h827),
    .in6(21'h828), .in7(21'h829), .in8(21'h829), .in9(21'h2082a), .in10(21'h2082c), .in11(21'h82d),
    .in12(21'h82e), .in13(21'h82f), .in14(21'ha0110), .in15(21'ha0111), .in16(21'h18c32), .in17(21'h40233),
    .in18(undriven), .in19(undriven), .in20(21'h120214), .in21(21'h120215), .in22(21'h120216),
    .in23(21'h120217), .in24(21'h120218), .in25(21'h120219), .in26(21'h13005a), .in27(21'h7485b),
    .in28(21'h3283c), .in29(21'h12183d), .in30(21'h9e), .in31(21'h14009f),
    .out({R1, R2, W, IMM, WB, RW, MEM_R, MEM_W, B, J, JR, ALU_SRC, ALUop}), .sel(Opcode));
endmodule

module IMMEDIATE_VALUE (
  input  [4:0] IMM_5,
  input  [7:0] IMM_8,
  input  [1:0] SEL,
  output [31:0] TO_ALU,
  output [31:0] SET
);

  wire [31:0] bit_extender_1_out, bit_extender_2_out, bit_extender_3_out;

  assign bit_extender_1_out = {{27{1'b0}}, IMM_5};  // Bit_Extender bit_extender_1
  assign bit_extender_2_out = {{27{IMM_5[4]}}, IMM_5};  // Bit_Extender bit_extender_2
  assign bit_extender_3_out = {{24{1'b0}}, IMM_8};  // Bit_Extender bit_extender_3
  assign SET = {{24{IMM_8[7]}}, IMM_8};  // Bit_Extender bit_extender_4
  Multiplexer #(.select(2), .width(32)) multiplexer_1 (
    .in0(bit_extender_1_out), .in1(bit_extender_2_out), .in2(bit_extender_3_out), .in3(SET), .out(TO_ALU),
    .sel(SEL), .en(1'b1));
endmodule

module SSET (
  input  [7:0] IMM_8,
  input  [31:0] ALU_RES,
  output [31:0] SSET
);


  assign SSET = {ALU_RES[31:8], IMM_8};
endmodule

module WRITE_BACK_TO_REG (
  input  [31:0] MEM,
  input  [31:0] ALU,
  input  [31:0] SSET,
  input  [31:0] SET,
  input  [3:0] WB,
  input  [31:0] JALR,
  output [31:0] back_to_reg
);

  Multiplexer #(.select(4), .width(32)) multiplexer_1 (
    .in0(ALU), .in1(SSET), .in2(SET), .in3({32{1'b0}}), .in4(JALR), .in5({32{1'b0}}), .in6({32{1'b0}}),
    .in7({32{1'b0}}), .in8(MEM), .in9({32{1'b0}}), .in10({32{1'b0}}), .in11({32{1'b0}}), .in12({32{1'b0}}),
    .in13({32{1'b0}}), .in14({32{1'b0}}), .in15({32{1'b0}}), .out(back_to_reg), .sel(WB), .en(1'b1));
endmodule

module MUX_3_8 (
  input  [31:0] Data0,
  input  [31:0] Data2,
  input  [31:0] Data2_2,
  input  [31:0] Data3,
  input  [31:0] Data4,
  input  [31:0] Data5,
  input  s2,
  input  s1,
  input  s0,
  input  [31:0] Data6,
  input  [31:0] Data7,
  output [31:0] out_12
);

  wire [31:0] multiplexer_1_out, multiplexer_2_out, multiplexer_3_out, multiplexer_4_out, multiplexer_5_out,
       multiplexer_6_out;

  Multiplexer #(.width(32), .enable("false")) multiplexer_1 (
    .in0(Data0), .in1(Data2), .out(multiplexer_1_out), .sel(s0));
  Multiplexer #(.width(32), .enable("false")) multiplexer_2 (
    .in0(Data2_2), .in1(Data3), .out(multiplexer_2_out), .sel(s0));
  Multiplexer #(.width(32), .enable("false")) multiplexer_3 (
    .in0(Data4), .in1(Data5), .out(multiplexer_3_out), .sel(s0));
  Multiplexer #(.width(32), .enable("false")) multiplexer_4 (
    .in0(Data6), .in1(Data7), .out(multiplexer_4_out), .sel(s0));
  Multiplexer #(.width(32), .enable("false")) multiplexer_5 (
    .in0(multiplexer_1_out), .in1(multiplexer_2_out), .out(multiplexer_5_out), .sel(s1));
  Multiplexer #(.width(32), .enable("false")) multiplexer_6 (
    .in0(multiplexer_3_out), .in1(multiplexer_4_out), .out(multiplexer_6_out), .sel(s1));
  Multiplexer #(.width(32), .enable("false")) multiplexer_7 (
    .in0(multiplexer_5_out), .in1(multiplexer_6_out), .out(out_12), .sel(s2));
endmodule
